# Fritzing sketch Equema3 (saved by Fritzing 0.9.3b)
breadboards: 1

parts:
  LED1 = LED - 5mm [color="Infrared (940nm)" package="5 mm [THT]"]
  Componente3 = Arduino Uno (Rev3)
  Q1 = PNP-Transistor [package="TO92 [THT]"]
  Q2 = PNP-Transistor [package="TO92 [THT]"]
  Q3 = PNP-Transistor [package="TO92 [THT]"]
  Q4 = PNP-Transistor [package="TO92 [THT]"]
  Q5 = PNP-Transistor [package="TO92 [THT]"]
  Q6 = PNP-Transistor [package="TO92 [THT]"]
  Q7 = PNP-Transistor [package="TO92 [THT]"]
  R1 = Resistor [tolerance=±5% resistance=220 package=THT]
  Q8 = PNP-Transistor [package="TO92 [THT]"]
  Q9 = PNP-Transistor [package="TO92 [THT]"]
  Q10 = PNP-Transistor [package="TO92 [THT]"]
  R2 = Resistor [tolerance=±5% resistance=10k package=THT]
  R3 = Resistor [tolerance=±5% resistance=10k package=THT]
  R4 = Resistor [tolerance=±5% resistance=10k package=THT]
  R5 = Resistor [tolerance=±5% resistance=10k package=THT]
  R6 = Resistor [tolerance=±5% resistance=10k package=THT]
  R7 = Resistor [tolerance=±5% resistance=10k package=THT]
  R8 = Resistor [tolerance=±5% resistance=10k package=THT]
  R9 = Resistor [tolerance=±5% resistance=10k package=THT]
  R10 = Resistor [tolerance=±5% resistance=10k package=THT]
  R11 = Resistor [tolerance=±5% resistance=10k package=THT]

nets:
  N1: LED1.cathode, R1.Pin_1
  N2: LED1.anode, Componente3.D12/MISO
  N3: Componente3.D8, Q6.C
  N4: Componente3.D9_PWM, Q8.C
  N5: Componente3.D10_PWM/SS, Q9.C
  N6: Componente3.D11_PWM/MOSI, Q10.C
  N7: Componente3.D2, Q2.C
  N8: Componente3.D3_PWM, Q4.C
  N9: Componente3.D4, Q3.C
  N10: Componente3.D5_PWM, Q5.C
  N11: Componente3.D6_PWM, Q7.C
  N12: Componente3.D7, Q1.C
  N13: Componente3.5V, Q1.E, Q2.E, Q3.E, Q4.E, Q5.E, Q6.E, Q7.E, Q8.E, Q9.E, Q10.E
  N14: Componente3.GND, R1.Pin_0
  N15: Q1.B, R7.Pin_1
  N16: Q2.B, R2.Pin_1
  N17: Q3.B, R4.Pin_1
  N18: Q4.B, R3.Pin_1
  N19: Q5.B, R5.Pin_1
  N20: Q6.B, R8.Pin_1
  N21: Q7.B, R6.Pin_1
  N22: Q8.B, R9.Pin_1
  N23: Q9.B, R10.Pin_1
  N24: Q10.B, R11.Pin_1

notes:
  Rotational control
  control of movements
  IR Emitter
