# Fritzing sketch Equema4 (saved by Fritzing 0.9.3b)
breadboards: 4

parts:
  LED273 = LED - 5mm [color="White (8000K)" package="5 mm [THT]"]  # not connected
  LED274 = LED - 5mm [color="White (8000K)" package="5 mm [THT]"]  # not connected
  LED275 = LED - 5mm [color="White (8000K)" package="5 mm [THT]"]  # not connected
  LED276 = LED - 5mm [color="White (8000K)" package="5 mm [THT]"]  # not connected
  LED277 = LED - 5mm [color="White (8000K)" package="5 mm [THT]"]  # not connected
  LED278 = LED - 5mm [color="White (8000K)" package="5 mm [THT]"]  # not connected
  LED279 = LED - 5mm [color="White (8000K)" package="5 mm [THT]"]  # not connected
  LED280 = LED - 5mm [color="White (8000K)" package="5 mm [THT]"]
  LED282 = LED - 5mm [color="White (8000K)" package="5 mm [THT]"]  # not connected
  LED283 = LED - 5mm [color="White (8000K)" package="5 mm [THT]"]
  LED284 = LED - 5mm [color="White (8000K)" package="5 mm [THT]"]  # not connected
  LED285 = LED - 5mm [color="White (8000K)" package="5 mm [THT]"]
  LED286 = LED - 5mm [color="White (8000K)" package="5 mm [THT]"]
  LED287 = LED - 5mm [color="White (8000K)" package="5 mm [THT]"]  # not connected
  LED288 = LED - 5mm [color="White (8000K)" package="5 mm [THT]"]  # not connected
  LED289 = LED - 5mm [color="White (8000K)" package="5 mm [THT]"]
  LED290 = LED - 5mm [color="White (8000K)" package="5 mm [THT]"]  # not connected
  LED291 = LED - 5mm [color="White (8000K)" package="5 mm [THT]"]  # not connected
  LED292 = LED - 5mm [color="White (8000K)" package="5 mm [THT]"]  # not connected
  LED293 = LED - 5mm [color="White (8000K)" package="5 mm [THT]"]  # not connected
  LED294 = LED - 5mm [color="White (8000K)" package="5 mm [THT]"]  # not connected
  LED295 = LED - 5mm [color="White (8000K)" package="5 mm [THT]"]  # not connected
  LED296 = LED - 5mm [color="White (8000K)" package="5 mm [THT]"]
  LED297 = LED - 5mm [color="White (8000K)" package="5 mm [THT]"]  # not connected
  LED298 = LED - 5mm [color="White (8000K)" package="5 mm [THT]"]
  LED299 = LED - 5mm [color="White (8000K)" package="5 mm [THT]"]
  LED305 = LED - 5mm [color="White (8000K)" package="5 mm [THT]"]  # not connected
  LED306 = LED - 5mm [color="White (8000K)" package="5 mm [THT]"]  # not connected
  LED307 = LED - 5mm [color="White (8000K)" package="5 mm [THT]"]  # not connected
  LED308 = LED - 5mm [color="White (8000K)" package="5 mm [THT]"]  # not connected
  LED309 = LED - 5mm [color="White (8000K)" package="5 mm [THT]"]  # not connected
  LED310 = LED - 5mm [color="White (8000K)" package="5 mm [THT]"]  # not connected
  LED311 = LED - 5mm [color="White (8000K)" package="5 mm [THT]"]  # not connected
  LED312 = LED - 5mm [color="White (8000K)" package="5 mm [THT]"]  # not connected
  LED313 = LED - 5mm [color="White (8000K)" package="5 mm [THT]"]  # not connected
  LED314 = LED - 5mm [color="White (8000K)" package="5 mm [THT]"]  # not connected
  LED315 = LED - 5mm [color="White (8000K)" package="5 mm [THT]"]  # not connected
  LED316 = LED - 5mm [color="White (8000K)" package="5 mm [THT]"]  # not connected
  LED317 = LED - 5mm [color="White (8000K)" package="5 mm [THT]"]  # not connected
  LED318 = LED - 5mm [color="White (8000K)" package="5 mm [THT]"]  # not connected
  LED319 = LED - 5mm [color="White (8000K)" package="5 mm [THT]"]
  LED320 = LED - 5mm [color="White (8000K)" package="5 mm [THT]"]  # not connected
  LED321 = LED - 5mm [color="White (8000K)" package="5 mm [THT]"]  # not connected
  LED322 = LED - 5mm [color="White (8000K)" package="5 mm [THT]"]  # not connected
  LED323 = LED - 5mm [color="White (8000K)" package="5 mm [THT]"]  # not connected
  LED324 = LED - 5mm [color="White (8000K)" package="5 mm [THT]"]  # not connected
  LED325 = LED - 5mm [color="White (8000K)" package="5 mm [THT]"]  # not connected
  LED326 = LED - 5mm [color="White (8000K)" package="5 mm [THT]"]  # not connected
  LED327 = LED - 5mm [color="White (8000K)" package="5 mm [THT]"]
  LED328 = LED - 5mm [color="White (8000K)" package="5 mm [THT]"]  # not connected
  LED329 = LED - 5mm [color="White (8000K)" package="5 mm [THT]"]  # not connected
  LED330 = LED - 5mm [color="White (8000K)" package="5 mm [THT]"]  # not connected
  LED331 = LED - 5mm [color="White (8000K)" package="5 mm [THT]"]  # not connected
  LED332 = LED - 5mm [color="White (8000K)" package="5 mm [THT]"]  # not connected
  LED333 = LED - 5mm [color="White (8000K)" package="5 mm [THT]"]  # not connected
  LED334 = LED - 5mm [color="White (8000K)" package="5 mm [THT]"]  # not connected
  LED335 = LED - 5mm [color="White (8000K)" package="5 mm [THT]"]
  LED336 = LED - 5mm [color="White (8000K)" package="5 mm [THT]"]  # not connected
  LED337 = LED - 5mm [color="White (8000K)" package="5 mm [THT]"]  # not connected
  LED338 = LED - 5mm [color="White (8000K)" package="5 mm [THT]"]  # not connected
  LED339 = LED - 5mm [color="White (8000K)" package="5 mm [THT]"]  # not connected
  LED340 = LED - 5mm [color="White (8000K)" package="5 mm [THT]"]  # not connected
  LED341 = LED - 5mm [color="White (8000K)" package="5 mm [THT]"]  # not connected
  LED342 = LED - 5mm [color="White (8000K)" package="5 mm [THT]"]  # not connected
  LED343 = LED - 5mm [color="White (8000K)" package="5 mm [THT]"]
  LED344 = LED - 5mm [color="White (8000K)" package="5 mm [THT]"]  # not connected
  LED345 = LED - 5mm [color="White (8000K)" package="5 mm [THT]"]
  LED346 = LED - 5mm [color="White (8000K)" package="5 mm [THT]"]
  LED347 = LED - 5mm [color="White (8000K)" package="5 mm [THT]"]
  LED348 = LED - 5mm [color="White (8000K)" package="5 mm [THT]"]
  LED349 = LED - 5mm [color="White (8000K)" package="5 mm [THT]"]
  R1 = Resistor [tolerance=±5% resistance=150 package=THT]
  R2 = Resistor [tolerance=±5% resistance=150 package=THT]
  R3 = Resistor [tolerance=±5% resistance=150 package=THT]
  R4 = Resistor [tolerance=±5% resistance=150 package=THT]
  R5 = Resistor [tolerance=±5% resistance=150 package=THT]
  R6 = Resistor [tolerance=±5% resistance=150 package=THT]
  R7 = Resistor [tolerance=±5% resistance=150 package=THT]
  R8 = Resistor [tolerance=±5% resistance=150 package=THT]
  R9 = Resistor [tolerance=±5% resistance=150 package=THT]
  R10 = Resistor [tolerance=±5% resistance=150 package=THT]
  R11 = Resistor [tolerance=±5% resistance=150 package=THT]
  R12 = Resistor [tolerance=±5% resistance=150 package=THT]
  R13 = Resistor [tolerance=±5% resistance=150 package=THT]
  R14 = Resistor [tolerance=±5% resistance=150 package=THT]
  R15 = Resistor [tolerance=±5% resistance=150 package=THT]
  R16 = Resistor [tolerance=±5% resistance=150 package=THT]
  R17 = Resistor [tolerance=±5% resistance=150 package=THT]
  R18 = Resistor [tolerance=±5% resistance=150 package=THT]
  R19 = Resistor [tolerance=±5% resistance=150 package=THT]
  R20 = Resistor [tolerance=±5% resistance=150 package=THT]
  R21 = Resistor [tolerance=±5% resistance=150 package=THT]
  R22 = Resistor [tolerance=±5% resistance=150 package=THT]
  R23 = Resistor [tolerance=±5% resistance=150 package=THT]
  R24 = Resistor [tolerance=±5% resistance=150 package=THT]
  R25 = Resistor [tolerance=±5% resistance=150 package=THT]
  R26 = Resistor [tolerance=±5% resistance=150 package=THT]
  R27 = Resistor [tolerance=±5% resistance=150 package=THT]
  R28 = Resistor [tolerance=±5% resistance=150 package=THT]
  R29 = Resistor [tolerance=±5% resistance=150 package=THT]
  R30 = Resistor [tolerance=±5% resistance=150 package=THT]
  R31 = Resistor [tolerance=±5% resistance=150 package=THT]
  R32 = Resistor [tolerance=±5% resistance=150 package=THT]
  R33 = Resistor [tolerance=±5% resistance=150 package=THT]
  R34 = Resistor [tolerance=±5% resistance=150 package=THT]
  R35 = Resistor [tolerance=±5% resistance=150 package=THT]
  R36 = Resistor [tolerance=±5% resistance=150 package=THT]
  R37 = Resistor [tolerance=±5% resistance=150 package=THT]
  R38 = Resistor [tolerance=±5% resistance=150 package=THT]
  R39 = Resistor [tolerance=±5% resistance=150 package=THT]
  R40 = Resistor [tolerance=±5% resistance=150 package=THT]
  R41 = Resistor [tolerance=±5% resistance=150 package=THT]
  R42 = Resistor [tolerance=±5% resistance=150 package=THT]
  R43 = Resistor [tolerance=±5% resistance=150 package=THT]
  R44 = Resistor [tolerance=±5% resistance=150 package=THT]
  R45 = Resistor [tolerance=±5% resistance=150 package=THT]
  R46 = Resistor [tolerance=±5% resistance=150 package=THT]
  R47 = Resistor [tolerance=±5% resistance=150 package=THT]
  R48 = Resistor [tolerance=±5% resistance=150 package=THT]
  R49 = Resistor [tolerance=±5% resistance=150 package=THT]
  R50 = Resistor [tolerance=±5% resistance=150 package=THT]
  R51 = Resistor [tolerance=±5% resistance=150 package=THT]
  R52 = Resistor [tolerance=±5% resistance=150 package=THT]
  R53 = Resistor [tolerance=±5% resistance=150 package=THT]
  R54 = Resistor [tolerance=±5% resistance=150 package=THT]
  R55 = Resistor [tolerance=±5% resistance=150 package=THT]
  R56 = Resistor [tolerance=±5% resistance=150 package=THT]  # not connected
  R57 = Resistor [tolerance=±5% resistance=150 package=THT]
  R58 = Resistor [tolerance=±5% resistance=150 package=THT]
  R59 = Resistor [tolerance=±5% resistance=150 package=THT]
  R60 = Resistor [tolerance=±5% resistance=150 package=THT]
  R61 = Resistor [tolerance=±5% resistance=150 package=THT]
  R62 = Resistor [tolerance=±5% resistance=150 package=THT]  # not connected
  R63 = Resistor [tolerance=±5% resistance=150 package=THT]
  U2 = 74HC595 [package="DIP16 [THT]"]
  U7 = 74HC595 [package="DIP16 [THT]"]
  U6 = 74HC595 [package="DIP16 [THT]"]
  U5 = 74HC595 [package="DIP16 [THT]"]
  U4 = 74HC595 [package="DIP16 [THT]"]
  U1 = 74HC595 [package="DIP16 [THT]"]
  U3 = 74HC595 [package="DIP16 [THT]"]
  U8 = 74HC595 [package="DIP16 [THT]"]
  Componente1 = Arduino Uno (Rev3)
  R64 = Resistor [tolerance=±5% resistance=150 package=THT]
  IC2 = ULN2803A [package=THT]

nets:
  N1: LED280.anode, R11.Pin_0, R28.Pin_1
  N2: LED283.anode, R22.Pin_0
  N3: LED285.anode, R53.Pin_1, R54.Pin_0, R64.Pin_1
  N4: LED286.anode, R61.Pin_1
  N5: LED289.anode, R58.Pin_0
  N6: LED296.cathode, IC2.Out_8
  N7: LED296.anode, R6.Pin_1
  N8: LED298.cathode, IC2.Out_7
  N9: LED299.cathode, IC2.Out_6
  N10: LED319.anode, R39.Pin_1
  N11: LED327.anode, R7.Pin_1, R26.Pin_1, R37.Pin_0, R44.Pin_0
  N12: LED335.anode, R13.Pin_0, R20.Pin_1
  N13: LED343.anode, R28.Pin_0
  N14: LED345.cathode, IC2.Out_5
  N15: LED346.cathode, IC2.Out_4
  N16: LED347.cathode, IC2.Out_3
  N17: LED348.cathode, IC2.Out_2
  N18: LED349.cathode, IC2.Out_1
  N19: R1.Pin_0, U7.Q7
  N20: R2.Pin_0, R43.Pin_0, U7.Q6
  N21: R3.Pin_0, U7.Q5
  N22: R4.Pin_0, R5.Pin_1, R63.Pin_0, U7.Q4
  N23: R5.Pin_0, R9.Pin_1, R15.Pin_0, U1.Q7
  N24: R6.Pin_0, U7.Q0
  N25: R7.Pin_0, R12.Pin_1
  N26: R8.Pin_0, U7.Q2
  N27: R9.Pin_0, U4.Q3
  N28: R10.Pin_0, U6.Q4
  N29: R11.Pin_1, U6.Q0
  N30: R12.Pin_0, R16.Pin_0, U6.Q1
  N31: R13.Pin_1, R44.Pin_1
  N32: R14.Pin_0, U8.Q4
  N33: R15.Pin_1, R47.Pin_1
  N34: R17.Pin_0, U8.Q1
  N35: R18.Pin_0, R57.Pin_1
  N36: R18.Pin_1, R53.Pin_0
  N37: R19.Pin_0, U6.Q2
  N38: R20.Pin_0, U8.Q0
  N39: R21.Pin_0, R27.Pin_0, U5.Q4
  N40: R23.Pin_0, U8.Q5
  N41: R24.Pin_0, U8.Q3
  N42: R25.Pin_0, R38.Pin_1, U5.Q7
  N43: R26.Pin_0, U5.Q0
  N44: R29.Pin_0, U4.Q5
  N45: R30.Pin_0, U5.Q2
  N46: R31.Pin_0, U5.Q6
  N47: R32.Pin_0, U4.Q4
  N48: R33.Pin_0, U5.Q3
  N49: R34.Pin_0, R37.Pin_1, U4.Q6
  N50: R35.Pin_0, R38.Pin_0, R51.Pin_1, U5.Q1
  N51: R36.Pin_0, U4.Q7
  N52: R39.Pin_0, U4.Q0
  N53: R40.Pin_0, U4.Q1
  N54: R41.Pin_0, U3.Q1
  N55: R42.Pin_0, U3.Q6
  N56: R45.Pin_0, U3.Q7
  N57: R45.Pin_1, R59.Pin_1
  N58: R46.Pin_0, U3.Q2
  N59: R47.Pin_0, U3.Q5
  N60: R48.Pin_0, U3.Q3
  N61: R49.Pin_0, U7.Q1
  N62: R49.Pin_1, U1.Q6
  N63: R50.Pin_0, R51.Pin_0
  N64: R52.Pin_0, U1.Q0, R64.Pin_0
  N65: R52.Pin_1, U4.Q2
  N66: R54.Pin_1, U3.Q4
  N67: R55.Pin_0, R57.Pin_0, R58.Pin_1, U5.GND
  N68: R55.Pin_1, R60.Pin_0, R61.Pin_0
  N69: R59.Pin_0, U5.Q5
  N70: R63.Pin_1, U1.Q5
  GND: U2.GND, U2.OE, U1.GND, U1.OE, U3.GND, U3.OE
  N71: U2.Q7', U3.DS
  VCC: U2.MR, U2.VCC, U4.VCC, U1.MR, U1.VCC, U3.MR, U3.VCC
  N72: U2.SH_CP, U7.SH_CP, U6.SH_CP, U5.SH_CP, U4.SH_CP, U1.SH_CP, U3.SH_CP, U8.SH_CP, Componente1.D13/SCK
  N73: U2.DS, U1.Q7'
  GND_2: U7.GND, U7.OE, U6.OE, U5.OE, U4.OE, U8.OE, Componente1.GND, IC2.0V
  VCC_2: U7.MR, U6.MR, U6.VCC, U5.MR, U5.VCC, U4.MR, U8.MR, U8.VCC, Componente1.5V, IC2.COM_-_Common
  N74: U7.DS, U6.Q7'
  GND_3: U6.GND, U4.GND, U8.GND
  N75: U6.DS, U8.Q7'
  N76: U5.Q7', U8.DS
  N77: U5.DS, U4.Q7'
  N78: U4.DS, U3.Q7'
  N79: U1.ST_CP, Componente1.D12/MISO
  N80: U1.DS, Componente1.D11_PWM/MOSI
  N81: Componente1.D8, IC2.In_2
  N82: Componente1.D9_PWM, IC2.In_1
  N83: Componente1.D2, IC2.In_8
  N84: Componente1.D3_PWM, IC2.In_7
  N85: Componente1.D4, IC2.In_6
  N86: Componente1.D5_PWM, IC2.In_5
  N87: Componente1.D6_PWM, IC2.In_4
  N88: Componente1.D7, IC2.In_3

notes:
  64-58
  56-50
  48-42
  40-34
  32-26
  24-18
  64 colunas x 8 camadas
