// Logisim project projeto-circuito.circ as structural Verilog: 1 circuit, main circuit main
module main (
  input  [2:0] in_1,
  input  [2:0] in_2,
  input  in_3
);

  wire demultiplexer_1_out0, demultiplexer_1_out1, demultiplexer_1_out2, demultiplexer_1_out3,
       demultiplexer_1_out4, demultiplexer_1_out5, demultiplexer_1_out6, demultiplexer_1_out7,
       demultiplexer_2_out0, demultiplexer_2_out1, demultiplexer_2_out2, demultiplexer_2_out3,
       demultiplexer_2_out4, demultiplexer_2_out5, demultiplexer_2_out6, demultiplexer_2_out7;

  Demultiplexer #(.select(3)) demultiplexer_1 (
    .out0(demultiplexer_1_out0), .out1(demultiplexer_1_out1), .out2(demultiplexer_1_out2),
    .out3(demultiplexer_1_out3), .out4(demultiplexer_1_out4), .out5(demultiplexer_1_out5),
    .out6(demultiplexer_1_out6), .out7(demultiplexer_1_out7), .in(1'b1), .sel(in_1), .en(in_3));
  // AND_Gate and_1 has open pins: in0=demultiplexer_1_out0, in4=demultiplexer_2_out0, out=open
  // AND_Gate and_2 has open pins: in0=demultiplexer_1_out1, in4=demultiplexer_2_out0, out=open
  // AND_Gate and_3 has open pins: in0=demultiplexer_1_out2, in4=demultiplexer_2_out0, out=open
  // AND_Gate and_4 has open pins: in0=demultiplexer_1_out3, in4=demultiplexer_2_out0, out=open
  // AND_Gate and_5 has open pins: in0=demultiplexer_1_out4, in4=demultiplexer_2_out0, out=open
  // AND_Gate and_6 has open pins: in0=demultiplexer_1_out5, in4=demultiplexer_2_out0, out=open
  // AND_Gate and_7 has open pins: in0=demultiplexer_1_out6, in4=demultiplexer_2_out0, out=open
  // AND_Gate and_8 has open pins: in0=demultiplexer_1_out7, in4=demultiplexer_2_out0, out=open
  // AND_Gate and_9 has open pins: in0=demultiplexer_1_out0, in4=demultiplexer_2_out1, out=open
  // AND_Gate and_10 has open pins: in0=demultiplexer_1_out1, in4=demultiplexer_2_out1, out=open
  // AND_Gate and_11 has open pins: in0=demultiplexer_1_out2, in4=demultiplexer_2_out1, out=open
  // AND_Gate and_12 has open pins: in0=demultiplexer_1_out3, in4=demultiplexer_2_out1, out=open
  // AND_Gate and_13 has open pins: in0=demultiplexer_1_out4, in4=demultiplexer_2_out1, out=open
  // AND_Gate and_14 has open pins: in0=demultiplexer_1_out5, in4=demultiplexer_2_out1, out=open
  // AND_Gate and_15 has open pins: in0=demultiplexer_1_out6, in4=demultiplexer_2_out1, out=open
  // AND_Gate and_16 has open pins: in0=demultiplexer_1_out7, in4=demultiplexer_2_out1, out=open
  // AND_Gate and_17 has open pins: in0=demultiplexer_1_out0, in4=demultiplexer_2_out2, out=open
  // AND_Gate and_18 has open pins: in0=demultiplexer_1_out1, in4=demultiplexer_2_out2, out=open
  // AND_Gate and_19 has open pins: in0=demultiplexer_1_out2, in4=demultiplexer_2_out2, out=open
  // AND_Gate and_20 has open pins: in0=demultiplexer_1_out3, in4=demultiplexer_2_out2, out=open
  // AND_Gate and_21 has open pins: in0=demultiplexer_1_out4, in4=demultiplexer_2_out2, out=open
  // AND_Gate and_22 has open pins: in0=demultiplexer_1_out5, in4=demultiplexer_2_out2, out=open
  // AND_Gate and_23 has open pins: in0=demultiplexer_1_out6, in4=demultiplexer_2_out2, out=open
  // AND_Gate and_24 has open pins: in0=demultiplexer_1_out7, in4=demultiplexer_2_out2, out=open
  // AND_Gate and_25 has open pins: in0=demultiplexer_1_out0, in4=demultiplexer_2_out3, out=open
  // AND_Gate and_26 has open pins: in0=demultiplexer_1_out1, in4=demultiplexer_2_out3, out=open
  // AND_Gate and_27 has open pins: in0=demultiplexer_1_out2, in4=demultiplexer_2_out3, out=open
  // AND_Gate and_28 has open pins: in0=demultiplexer_1_out3, in4=demultiplexer_2_out3, out=open
  // AND_Gate and_29 has open pins: in0=demultiplexer_1_out4, in4=demultiplexer_2_out3, out=open
  // AND_Gate and_30 has open pins: in0=demultiplexer_1_out5, in4=demultiplexer_2_out3, out=open
  // AND_Gate and_31 has open pins: in0=demultiplexer_1_out6, in4=demultiplexer_2_out3, out=open
  // AND_Gate and_32 has open pins: in0=demultiplexer_1_out7, in4=demultiplexer_2_out3, out=open
  Demultiplexer #(.select(3)) demultiplexer_2 (
    .out0(demultiplexer_2_out0), .out1(demultiplexer_2_out1), .out2(demultiplexer_2_out2),
    .out3(demultiplexer_2_out3), .out4(demultiplexer_2_out4), .out5(demultiplexer_2_out5),
    .out6(demultiplexer_2_out6), .out7(demultiplexer_2_out7), .in(1'b1), .sel(in_2), .en(in_3));
  // AND_Gate and_33 has open pins: in0=demultiplexer_1_out0, in4=demultiplexer_2_out4, out=open
  // AND_Gate and_34 has open pins: in0=demultiplexer_1_out1, in4=demultiplexer_2_out4, out=open
  // AND_Gate and_35 has open pins: in0=demultiplexer_1_out2, in4=demultiplexer_2_out4, out=open
  // AND_Gate and_36 has open pins: in0=demultiplexer_1_out3, in4=demultiplexer_2_out4, out=open
  // AND_Gate and_37 has open pins: in0=demultiplexer_1_out4, in4=demultiplexer_2_out4, out=open
  // AND_Gate and_38 has open pins: in0=demultiplexer_1_out5, in4=demultiplexer_2_out4, out=open
  // AND_Gate and_39 has open pins: in0=demultiplexer_1_out6, in4=demultiplexer_2_out4, out=open
  // AND_Gate and_40 has open pins: in0=demultiplexer_1_out7, in4=demultiplexer_2_out4, out=open
  // AND_Gate and_41 has open pins: in0=demultiplexer_1_out0, in4=demultiplexer_2_out5, out=open
  // AND_Gate and_42 has open pins: in0=demultiplexer_1_out1, in4=demultiplexer_2_out5, out=open
  // AND_Gate and_43 has open pins: in0=demultiplexer_1_out2, in4=demultiplexer_2_out5, out=open
  // AND_Gate and_44 has open pins: in0=demultiplexer_1_out3, in4=demultiplexer_2_out5, out=open
  // AND_Gate and_45 has open pins: in0=demultiplexer_1_out4, in4=demultiplexer_2_out5, out=open
  // AND_Gate and_46 has open pins: in0=demultiplexer_1_out5, in4=demultiplexer_2_out5, out=open
  // AND_Gate and_47 has open pins: in0=demultiplexer_1_out6, in4=demultiplexer_2_out5, out=open
  // AND_Gate and_48 has open pins: in0=demultiplexer_1_out7, in4=demultiplexer_2_out5, out=open
  // AND_Gate and_49 has open pins: in0=demultiplexer_1_out0, in4=demultiplexer_2_out6, out=open
  // AND_Gate and_50 has open pins: in0=demultiplexer_1_out1, in4=demultiplexer_2_out6, out=open
  // AND_Gate and_51 has open pins: in0=demultiplexer_1_out2, in4=demultiplexer_2_out6, out=open
  // AND_Gate and_52 has open pins: in0=demultiplexer_1_out3, in4=demultiplexer_2_out6, out=open
  // AND_Gate and_53 has open pins: in0=demultiplexer_1_out4, in4=demultiplexer_2_out6, out=open
  // AND_Gate and_54 has open pins: in0=demultiplexer_1_out5, in4=demultiplexer_2_out6, out=open
  // AND_Gate and_55 has open pins: in0=demultiplexer_1_out6, in4=demultiplexer_2_out6, out=open
  // AND_Gate and_56 has open pins: in0=demultiplexer_1_out7, in4=demultiplexer_2_out6, out=open
  // AND_Gate and_57 has open pins: in0=demultiplexer_1_out0, in4=demultiplexer_2_out7, out=open
  // AND_Gate and_58 has open pins: in0=demultiplexer_1_out1, in4=demultiplexer_2_out7, out=open
  // AND_Gate and_59 has open pins: in0=demultiplexer_1_out2, in4=demultiplexer_2_out7, out=open
  // AND_Gate and_60 has open pins: in0=demultiplexer_1_out3, in4=demultiplexer_2_out7, out=open
  // AND_Gate and_61 has open pins: in0=demultiplexer_1_out4, in4=demultiplexer_2_out7, out=open
  // AND_Gate and_62 has open pins: in0=demultiplexer_1_out5, in4=demultiplexer_2_out7, out=open
  // AND_Gate and_63 has open pins: in0=demultiplexer_1_out6, in4=demultiplexer_2_out7, out=open
  // AND_Gate and_64 has open pins: in0=demultiplexer_1_out7, in4=demultiplexer_2_out7, out=open
endmodule
